# Fritzing sketch arduino-radiator-console (saved by Fritzing 0.9.3b)
breadboards: 1

parts:
  U1 = NodeMCU V1.0
  R1 = Resistor [tolerance=±5% resistance=220 package="0402 [SMD]"]
  R2 = Resistor [tolerance=±5% resistance=220 package="0402 [SMD]"]
  R3 = Resistor [tolerance=±5% resistance=220 package="0402 [SMD]"]
  R4 = Resistor [tolerance=±5% resistance=220 package="0402 [SMD]"]
  R5 = Resistor [tolerance=±5% resistance=220 package="0402 [SMD]"]
  R6 = Resistor [tolerance=±5% resistance=220 package="0402 [SMD]"]
  R7 = Resistor [tolerance=±5% resistance=220 package="0402 [SMD]"]
  LED1 = LED - 5mm [color="Red (633nm)" package="5 mm [THT]"]
  LED2 = LED - 5mm [color="Green (555nm)" package="5 mm [THT]"]
  LED3 = LED - 5mm [color="Red (633nm)" package="5 mm [THT]"]
  LED4 = LED - 5mm [color="Green (555nm)" package="5 mm [THT]"]
  LED5 = LED - 5mm [color="Green (555nm)" package="5 mm [THT]"]
  LED6 = LED - 5mm [color="Red (633nm)" package="5 mm [THT]"]
  LED7 = LED - 5mm [color="Red (633nm)" package="5 mm [THT]"]
  Part1 = Adafruit I2C+SPI LCD Backpack [part_number="Adafruit #292"]
  U2 = LCD-16X2 [package=lcd-16x2_nosilk]

nets:
  N1: U1.D0, R6.Pin_0
  N2: U1.D1, R1.Pin_0
  N3: U1.D2, Part1.DATA
  N4: U1.D3, Part1.LATCH
  N5: U1.D4, R2.Pin_0
  GND: U1.GND, LED1.cathode, LED2.cathode, LED3.cathode, LED4.cathode, LED5.cathode, LED6.cathode, LED7.cathode, Part1.GND, U2.VSS, U2.R_W
  N6: U1.D5, R3.Pin_0
  N7: U1.D6, R4.Pin_0
  N8: U1.D7, R5.Pin_0
  N9: U1.D8, R7.Pin_0
  VIN: U1.Vin, Part1.VCC, U2.VDD, U2.A
  N10: R1.Pin_1, LED6.anode
  N11: R2.Pin_1, LED5.anode
  N12: R3.Pin_1, LED1.anode
  N13: R4.Pin_1, LED2.anode
  N14: R5.Pin_1, LED3.anode
  N15: R6.Pin_1, LED7.anode
  N16: R7.Pin_1, LED4.anode
  N17: Part1.CONTRAST, U2.VO
  N18: Part1.RS, U2.RS
  N19: Part1.E, U2.E
  N20: Part1.DB0, U2.DB0
  N21: Part1.DB1, U2.DB1
  N22: Part1.DB2, U2.DB2
  N23: Part1.DB3, U2.DB3
  N24: Part1.DB4, U2.DB4
  N25: Part1.DB5, U2.DB5
  N26: Part1.DB6, U2.DB6
  N27: Part1.DB7, U2.DB7
  N28: Part1.LEDK, U2.K

custom parts:
  NodeMCU V1.0: ESP8266 based NodeMCU
  Adafruit I2C+SPI LCD Backpack: LCD backpacks reduce the number of pins needed to connect to an LCD. LCDs are a fun and easy way to have your microcontroller project talk back to you. Character LCDs are common, and easy to get, available in tons of colors and sizes. We've written tutorials on using character LCDs with an Arduino (or similar microcontroller) but find that the number of pins necessary to control the LCD can be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
